// Logisim project Domaci2_NILI_ORT1.circ as structural Verilog: 1 circuit, main circuit Sistem sa min.br.dvoulaznih NILIi log. kola
module Sistem_sa_min_br_dvoulaznih_NILIi_log__kola (
  input  a,
  input  b,
  input  c,
  input  d,
  input  e,
  output out_6
);

  wire nor_1_out, nor_2_out, nor_3_out, nor_4_out, nor_5_out, nor_6_out, nor_7_out, nor_8_out;

  nor nor_1 (nor_1_out, b, b);
  nor nor_2 (nor_2_out, e, e);
  nor nor_3 (nor_3_out, nor_1_out, nor_2_out);
  nor nor_4 (nor_4_out, nor_3_out, nor_3_out);
  nor nor_5 (nor_5_out, nor_4_out, d);
  nor nor_6 (nor_6_out, c, a);
  nor nor_7 (nor_7_out, nor_5_out, nor_5_out);
  nor nor_8 (nor_8_out, nor_6_out, nor_6_out);
  nor nor_9 (out_6, nor_7_out, nor_8_out);

  // Notes on the sheet:
  //   Kristina Sataric 555/2015
  //   Datum rodjenja: 22.05. , zbir cifara 9, tj. 01001
endmodule
