// Logisim project Logickokoloo.circ as structural Verilog: 1 circuit, main circuit LogickoKolo
module LogickoKolo (
  input  in_1,
  input  in_2,
  output out_3
);

  and and_1 (out_3, in_1, in_2);
endmodule
