// Logisim project logisimlogiskokolo1.circ as structural Verilog: 1 circuit, main circuit main
module main (
  input  x1,
  input  x2,
  output y
);

  wire not_1_out, not_2_out;

  not not_1 (not_1_out, x1);
  not not_2 (not_2_out, x2);
  and and_1 (y, not_1_out, not_2_out);
endmodule
